# Fritzing sketch Schematic (saved by Fritzing 0.9.3b)
breadboards: 1

parts:
  Raspberry_Pi_1 = Raspberry Pi 3 [part_number=RPI-3-V1.2]
  L2-1 = Arduino Nano (Rev3.0)
  L2-2 = Arduino Nano (Rev3.0)
  R1 = Resistor [tolerance=±5% resistance=220 package=THT]
  R2 = Resistor [tolerance=±5% resistance=220 package=THT]
  R3 = Resistor [tolerance=±5% resistance=220 package=THT]
  LED1 = LED - 5mm [color="Red (633nm)" package="5 mm [THT]"]
  LED2 = LED - 5mm [color="Red (633nm)" package="5 mm [THT]"]
  LED3 = LED - 5mm [color="Red (633nm)" package="5 mm [THT]"]
  J1 = Basic Servo
  J2 = Basic Servo
  VCC1 = 4 x AAA Battery Mount

nets:
  N1: Raspberry_Pi_1.GPIO2, L2-1.A4, L2-2.A4
  N2: Raspberry_Pi_1.GPIO3, L2-1.A5, L2-2.A5
  GND: L2-1.GND, L2-2.GND, LED1.cathode, LED2.cathode, LED3.cathode, J1.gnd, J2.gnd
  N3: L2-2.D3, J2.pulse
  N4: L2-2.D4, J1.pulse
  N5: L2-2.D11/MOSI, R3.Pin_0
  N6: L2-2.D12/MISO, R2.Pin_0
  N7: L2-2.D13/SCK, R1.Pin_0
  N8: R1.Pin_1, LED1.anode
  N9: R2.Pin_1, LED2.anode
  N10: R3.Pin_1, LED3.anode
  VCC: J1.vcc, J2.vcc, VCC1.+
